# Fritzing sketch sketch (saved by Fritzing 0.9.9b)
breadboards: 1

parts:
  Part1 = Arduino Nano 33 IOT
  R1 = Resistor [tolerance=±5% power=0.25 resistance=47k package=THT]
  R2 = Resistor [tolerance=±5% power=0.25 resistance=47k package=THT]
  Thermistor_#1 = Temperature Sensor (Thermistor) [package=THT]
  Thermistor_#0 = Temperature Sensor (Thermistor) [package=THT]

nets:
  N1: Part1.RESET, Part1.A7
  N2: Part1.GND, Part1.D13~, Thermistor_#1.pin_0, Thermistor_#0.pin_0
  N3: Part1.D11/MOSI, Part1.+5V
  N4: Part1.A1, R2.Pin_1, Thermistor_#1.pin_1
  N5: Part1.A0, R1.Pin_1, Thermistor_#0.pin_1
  N6: Part1.3V3, R1.Pin_0, R2.Pin_0

custom parts:
  Arduino Nano 33 IOT: The Arduino Nano 33 IoT is the easiest and cheapest point of entry to enhance existing devices (and creating new ones) to be part of the IoT and designing pico-network applications. Whether you are looking at building a sensor network connected to your office or home router, or if you want to create a BLE device sending data to a cellphone, the Nano 33 IoT is your one-stop-solution for many of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
  Temperature Sensor (Thermistor): A 50k NTC Thermistor (Temperature Sensor)
